# Fritzing sketch FreezerThermometer (saved by Fritzing 0.9.1b)
breadboards: 1

parts:
  Part1 = Arduino Uno (Rev3)
  T1 = LM35 Temperature Sensor [package="TO92 [THT]"]
  LCD1 = Adafruit Negative RGB 2x16 LCD

nets:
  N1: Part1.A1, T1.Vout
  N2: Part1.A4/SDA, LCD1.no_name_yet#13
  N3: Part1.A5/SCL, LCD1.no_name_yet#14
  N4: Part1.AREF, Part1.5V, T1.+Vs, LCD1.no_name_yet#3
  GND: Part1.GND, T1.GND, LCD1.no_name_yet#6

custom parts:
  Adafruit Negative RGB 2x16 LCD: Adafruit Negative 2x16 LCD Display with RGB Backlight
